# Fritzing sketch arduino-kiss (saved by Fritzing 0.9.2b)
perfboards: 1

parts:
  Part1 = Arduino Nano (Rev3.0)
  J1 = female pin header, 5 pins [form="♀ (female)"]
  J2 = female pin header, 5 pins [form="♀ (female)"]

nets:
  N1: Part1.GND, J1.pin5, J2.pin5
  N2: Part1.D2, J1.pin4
  N3: Part1.D10, J2.pin4
  N4: Part1.D11/MOSI, J2.pin2
  N5: Part1.D12/MISO, J2.pin3
  N6: Part1.3V3, J1.pin1, J2.pin1
  N7: Part1.D13/SCK, J1.pin2
